// Logisim project cpu.circ as structural Verilog: 1 circuit, main circuit cpu
module cpu (
);

  wire clk, isIMM, mips_ram_1_p5, registerfile_1_p4, RST, write;
  wire [1:0] regmux;
  wire [4:0] rs_addr, rt_addr;
  wire [5:0] funcode, opcode;
  wire [15:0] \总周期数 , \无条件分支指令数 , \有条件分支成功跳转 , \有条件分支指令数 ;
  wire [15:6] imm16;
  wire [31:0] alu_1_result, bit_extender_1_out, bit_extender_2_out, bit_extender_3_out, mips_ram_1_p3,
       multiplexer_1_out, multiplexer_2_out, multiplexer_3_out, PC_q, registerfile_1_p8, registerfile_1_p9,
       SyscallOut;

  Button \u_总复位  (.out(RST));
  Clock clock_1 (.out(clk));
  Register #(.width(32)) PC (.Q(PC_q), .clk(clk));  // open: D, en, clr
  Hex_Digit_Display hex_digit_display_1 (.value(SyscallOut[31:28]));  // open: dp
  Hex_Digit_Display hex_digit_display_2 (.value(SyscallOut[27:24]));  // open: dp
  Hex_Digit_Display hex_digit_display_3 (.value(SyscallOut[23:20]));  // open: dp
  Hex_Digit_Display hex_digit_display_4 (.value(SyscallOut[19:16]));  // open: dp
  Hex_Digit_Display hex_digit_display_5 (.value(SyscallOut[11:8]));  // open: dp
  Hex_Digit_Display hex_digit_display_6 (.value(SyscallOut[15:12]));  // open: dp
  ROM #(.addrWidth(24), .dataWidth(32)) rom_1 (
    .addr(PC_q[25:2]), .data({opcode, rs_addr, rt_addr, imm16, funcode}));  // open: sel
  Hex_Digit_Display hex_digit_display_7 (.value(SyscallOut[3:0]));  // open: dp
  Hex_Digit_Display hex_digit_display_8 (.value(SyscallOut[7:4]));  // open: dp
  assign bit_extender_1_out = {{16{imm16[15]}}, {imm16, funcode}};  // Bit_Extender bit_extender_1
  Multiplexer #(.select(2), .width(32), .disabled(0), .enable("false")) multiplexer_1 (
    .in0(alu_1_result), .in1(PC_q), .in2(multiplexer_3_out), .out(multiplexer_1_out), .sel(regmux));  // open: in3
  // Probe on \总周期数 
  // Probe on \无条件分支指令数 
  // Probe on \有条件分支指令数 
  // Probe on \有条件分支成功跳转 
  // RegisterFile registerfile_1: pin names not known; wires that end beside it: multiplexer_1_out, clk, write, registerfile_1_p4, registerfile_1_p4, rs_addr, rt_addr, registerfile_1_p8, registerfile_1_p9, registerfile_1_p9
  Multiplexer #(.width(32), .enable("false")) multiplexer_2 (
    .in0(registerfile_1_p9), .in1(bit_extender_1_out), .out(multiplexer_2_out), .sel(isIMM));
  ALU alu_1 (
    .X(registerfile_1_p8), .Result(alu_1_result), .Y(multiplexer_2_out), .shamt(imm16[10:6]));  // open: AluOP, Equal, Signed_Overflow, Result_2, UnSigned_Overflow
  // MIPS_RAM mips_ram_1: pin names not known; wires that end beside it: alu_1_result[25:2], registerfile_1_p8, mips_ram_1_p3, alu_1_result[1], mips_ram_1_p5
  assign bit_extender_2_out = {{16{1'b0}}, mips_ram_1_p3[15:0]};  // Bit_Extender bit_extender_2
  assign bit_extender_3_out = {{16{1'b0}}, mips_ram_1_p3[31:16]};  // Bit_Extender bit_extender_3
  Multiplexer #(.select(2), .width(32)) multiplexer_3 (
    .in0(mips_ram_1_p3), .in2(bit_extender_2_out), .in3(bit_extender_3_out), .out(multiplexer_3_out),
    .en(mips_ram_1_p5));  // open: in1, sel

  // Other names for the same wires on the sheet: imm16[5:0] = funcode; shamt[4:0] = imm16[10:6];
  //   rd_addr[4:0] = imm16[15:11]

  // Notes on the sheet:
  //   数码管输出应该用寄存器锁存，否则显示数据只能一闪而过
  //   可以通过项目增加Logisim库的方式将前几次实验完成的电路作为子电路引入到本电路中使用
  //   数码管输出
  //   总复位信号应将除ROM以外所有存储组件全部清零
endmodule
